// Logisim project cpu_logisim.circ as structural Verilog
module memory_io (
);

  wire MEMload, MEMresult, not_1_out;
  wire [14:0] adr;

  not not_1 (not_1_out, MEMload);
  RAM #(.addrWidth(15), .databus("bidir")) IC1 (.addr(adr), .we(not_1_out), .oe(MEMresult));  // open: clk, data
  ROM #(.addrWidth(15)) IC2 (.addr(adr));  // open: data
endmodule
